# Fritzing sketch steampunk-clock (saved by Fritzing 1.0.6)
circuit board: 8.46667cm x 5.64444cm
perfboards: 1

parts:
  WeMos_D1_Mini1 = WeMos D1 Mini
  ZS-042_RTC1 = ZS-042 RTC Module
  Hour_servo = Dagu DGServo 9g (Top view) [part_number=RS001B]
  Minute_servo = Dagu DGServo 9g (Top view) [part_number=RS001B]
  Buzzer = Piezo Buzzer
  Settings_button = Momentary Switch [package=ksa_sealed_tac_switch]
  Hour_led = LED - 5mm [color="Yellow (595nm)" current=0.030A package="5 mm [THT]"]
  R1 = Resistor [tolerance=±5% power=0.25W resistance=100 package=THT]
  Minute_led = LED - 5mm [color="Yellow (595nm)" current=0.030A package="5 mm [THT]"]
  R2 = Resistor [tolerance=±5% power=0.25W resistance=100 package=THT]
  M1 = pcf8574 io expansion board [package=THT]
  Hours = female pin header, 4 pins [form="♀ (female)"]
  Minutes = female pin header, 4 pins [form="♀ (female)"]
  Mode_switch = SWITCH-SP3T [package=switch-sp3t-smd]
  Hour_cable = Header 4 [package=1x04-1mm-ra]
  Minute_cable = Header 4 [package=1x04-1mm-ra]

nets (from the schematic view):
  VCC: WeMos_D1_Mini1.3V3, ZS-042_RTC1.VCC, M1.VCC, Mode_switch.3
  N1: WeMos_D1_Mini1.D0, Hours.pin4
  N2: WeMos_D1_Mini1.D1, ZS-042_RTC1.SCL, M1.SCL
  N3: WeMos_D1_Mini1.D2, ZS-042_RTC1.SDA, M1.SDA
  N4: WeMos_D1_Mini1.D3, Buzzer.pin_2
  N5: WeMos_D1_Mini1.D5, Minutes.pin4
  N6: WeMos_D1_Mini1.D6, R1.Pin_1
  N7: WeMos_D1_Mini1.D7, R2.Pin_1
  GND: WeMos_D1_Mini1.G, ZS-042_RTC1.GND, Buzzer.pin_1, Settings_button.1, M1.GND, Hours.pin2, Minutes.pin2
  N8: Hour_servo.gnd, Hour_led.cathode, Hour_cable.2
  N9: Hour_servo.vcc, Hour_cable.3
  N10: Hour_servo.pulse, Hour_cable.4
  N11: Minute_servo.gnd, Minute_led.cathode, Minute_cable.2
  N12: Minute_servo.vcc, Minute_cable.3
  N13: Minute_servo.pulse, Minute_cable.4
  N14: Settings_button.4, M1.O3
  N15: Hour_led.anode, Hour_cable.1
  N16: R1.Pin_0, Hours.pin1
  N17: Minute_led.anode, Minute_cable.1
  N18: R2.Pin_0, Minutes.pin1
  N19: M1.O0, Mode_switch.1
  N20: M1.O1, Mode_switch.2
  N21: M1.O2, Mode_switch.4
  N22: Hours.pin3, Minutes.pin3

custom parts:
  Piezo Buzzer: Part from https://www.nutsvolts.com/magazine/article/november2012_SmileysWorkshop. Breadboard and icon images modified to be 0.3" in spacing and be more similar to the actual physical part.
  pcf8574 io expansion board: pcf8574 io expansion board.
